# Fritzing sketch ControlBoard (saved by Fritzing 0.9.2b)
perfboards: 2

parts:
  J1 = female pin header, 12 pins [form="♀ (female)"]  # not connected
  J2 = female pin header, 12 pins [form="♀ (female)"]
  J3 = female pin header, 6 pins [form="♀ (female)"]
  J4 = female pin header, 6 pins [form="♀ (female)"]
  Redbear_DUO = IC, DIP package, 24 pins [chip_label="Redbear DUO"]
  J5 = female pin header, 4 pins [form="♀ (female)"]  # not connected
  BLE_Nano = IC, DIP package, 12 pins [chip_label="BLE Nano"]  # not connected
  J6 = female pin header, 12 pins [form="♀ (female)"]  # not connected
  J7 = female pin header, 12 pins [form="♀ (female)"]  # not connected
  J8 = female pin header, 6 pins [form="♀ (female)"]
  J9 = female pin header, 6 pins [form="♀ (female)"]  # not connected
  J10 = female pin header, 4 pins [form="♀ (female)"]

nets:
  N1: J2.pin2, J3.pin2
  N2: J4.pin1, Redbear_DUO.pin18
  N3: J8.pin5, J10.pin3
  N4: J8.pin6, J10.pin4
