# Fritzing sketch Mainboard (saved by Fritzing 0.9.2b)
circuit board: 6.96472cm x 4.85cm
perfboards: 1

parts:
  Atmega32 = ATmega644 [package=pdpi]
  U5 = IC, SIP package, 4 pins [chip_label=5V part_number=D24V6F5]  # not connected
  Bauteil2 = Motor Driver 1A Dual TB6612FNG  # not connected
  5v_Step = female pin header, 4 pins [form="♀ (female)"]
  J3 = female pin header, 6 pins [form="♀ (female)"]
  Main_Motor = female pin header, 6 pins [form="♀ (female)"]
  U6 = IC, DIP package, 12 pins [chip_label=DRV8801]  # not connected
  Feature_Motors = female pin header, 8 pins [form="♀ (female)"]
  J6 = female pin header, 8 pins [form="♀ (female)"]
  Power = female pin header, 2 pins [form="♀ (female)"]
  Capacitor = Capacitor [package=cap-pth-small2]
  Capacitor_2 = Capacitor [package=cap-pth-small2]
  XTAL = Crystal [frequency="16 Mhz" package=THT]
  Control_board = female pin header, 4 pins [form="♀ (female)"]
  LEDs = female pin header, 12 pins [form="♀ (female)"]
  J14 = female pin header, 12 pins [form="♀ (female)"]
  RGB = female pin header, 4 pins [form="♀ (female)"]
  Feat1 = female pin header, 2 pins [form="♀ (female)"]
  Feat2 = female pin header, 2 pins [form="♀ (female)"]
  Main = female pin header, 2 pins [form="♀ (female)"]
  Servo = female pin header, 3 pins [form="♀ (female)"]
  J19 = female pin header, 5 pins [form="♀ (female)"]
  Flash = female pin header, 5 pins [form="♀ (female)"]
  R1 = Resistor [tolerance=±5% resistance=220 package="0402 [SMD]"]
  R2 = Resistor [tolerance=±5% resistance=220 package="0402 [SMD]"]
  R3 = Resistor [tolerance=±5% resistance=220 package="0402 [SMD]"]
  R4 = Resistor [tolerance=±5% resistance=220 package="0402 [SMD]"]
  R5 = Resistor [tolerance=±5% resistance=220 package="0402 [SMD]"]
  R6 = Resistor [tolerance=±5% resistance=220 package="0402 [SMD]"]
  R7 = Resistor [tolerance=±5% resistance=220 package="0402 [SMD]"]
  R8 = Resistor [tolerance=±5% resistance=220 package="0402 [SMD]"]
  R9 = Resistor [tolerance=±5% resistance=220 package="0402 [SMD]"]
  R10 = Resistor [tolerance=±5% resistance=220 package="0402 [SMD]"]
  R11 = Resistor [tolerance=±5% resistance=220 package="0402 [SMD]"]
  R12 = Resistor [tolerance=±5% resistance=220 package="0402 [SMD]"]
  R15 = Resistor [tolerance=±5% resistance=220 package="0402 [SMD]"]
  R14 = Resistor [tolerance=±5% resistance=220 package="0402 [SMD]"]
  R13 = Resistor [tolerance=±5% resistance=220 package="0402 [SMD]"]
  VDD = female pin header, 1 pin [form="♀ (female)"]  # not connected
  GND = female pin header, 1 pin [form="♀ (female)"]  # not connected
  GND_2 = female pin header, 1 pin [form="♀ (female)"]  # not connected
  VM = female pin header, 1 pin [form="♀ (female)"]  # not connected

nets:
  N1: Atmega32.PB0, R12.Pin_0, R15.Pin_0
  N2: Atmega32.PB1, R14.Pin_0, R13.Pin_0
  N3: Atmega32.PB3, Servo.pin3
  N4: Atmega32.PB5, J19.pin1
  N5: Atmega32.PB6, J19.pin5
  N6: Atmega32.PB7, J19.pin4
  N7: Atmega32.RESET, J19.pin3
  N8: Atmega32.VCC, Atmega32.AVCC, 5v_Step.pin1, J3.pin1, Feature_Motors.pin2, J6.pin4, Capacitor.2, Capacitor_2.2, Control_board.pin1, Servo.pin2
  N9: Atmega32.GND, 5v_Step.pin2, J3.pin6, Main_Motor.pin6, Feature_Motors.pin3, Feature_Motors.pin8, J6.pin8, Power.pin1, Capacitor.1, Capacitor_2.1, Control_board.pin2, J14.pin1, J14.pin2, J14.pin3, J14.pin4, J14.pin5, J14.pin6, J14.pin7, J14.pin8, J14.pin9, J14.pin10, J14.pin11, J14.pin12, RGB.pin2, Servo.pin1, Flash.pin2, Flash.pin3, Flash.pin4, Flash.pin5
  N10: Atmega32.XTAL2, XTAL.pin_1
  N11: Atmega32.XTAL1, XTAL.pin_0
  N12: Atmega32.PD0, Control_board.pin3
  N13: Atmega32.PD1, Control_board.pin4
  N14: Atmega32.PD2, J6.pin5
  N15: Atmega32.PD3, J6.pin6
  N16: Atmega32.PD4, J6.pin7
  N17: Atmega32.PD5, J3.pin5
  N18: Atmega32.PD6, J3.pin4
  N19: Atmega32.PD7, J6.pin1
  N20: Atmega32.PC0, J6.pin2
  N21: Atmega32.PC1, J6.pin3
  N22: Atmega32.PC6, R11.Pin_0
  N23: Atmega32.PC7, R10.Pin_0
  N24: Atmega32.PA5, R8.Pin_0, R9.Pin_0
  N25: Atmega32.PA4, R6.Pin_0, R7.Pin_0
  N26: Atmega32.PA3, R4.Pin_0, R5.Pin_0
  N27: Atmega32.PA2, R3.Pin_0
  N28: Atmega32.PA1, R2.Pin_0
  N29: Atmega32.PA0, R1.Pin_0
  N30: 5v_Step.pin3, 5v_Step.pin4, Main_Motor.pin3, Feature_Motors.pin1, Power.pin2
  N31: Main_Motor.pin4, Main.pin1
  N32: Main_Motor.pin5, Main.pin2
  N33: Feature_Motors.pin4, Feat1.pin2
  N34: Feature_Motors.pin5, Feat1.pin1
  N35: Feature_Motors.pin6, Feat2.pin2
  N36: Feature_Motors.pin7, Feat2.pin1
  N37: LEDs.pin1, R4.Pin_1
  N38: LEDs.pin2, R5.Pin_1
  N39: LEDs.pin3, R6.Pin_1
  N40: LEDs.pin4, R7.Pin_1
  N41: LEDs.pin5, R8.Pin_1
  N42: LEDs.pin6, R9.Pin_1
  N43: LEDs.pin7, R10.Pin_1
  N44: LEDs.pin8, R11.Pin_1
  N45: LEDs.pin9, R12.Pin_1
  N46: LEDs.pin10, R15.Pin_1
  N47: LEDs.pin11, R14.Pin_1
  N48: LEDs.pin12, R13.Pin_1
  N49: RGB.pin1, R1.Pin_1
  N50: RGB.pin3, R2.Pin_1
  N51: RGB.pin4, R3.Pin_1

notes:
  R
  GN
  G
  B
  FRO
  BLL
  BLR
  FL
  FR
  REV
  REA
  5V
  RX
  TX
  GND
  12V
  lego control mainboard
