# Fritzing sketch ControlBoard (saved by Fritzing 0.9.2b)
perfboards: 2

parts:
  J1 = female pin header, 12 pins [form="♀ (female)"]
  J2 = female pin header, 12 pins [form="♀ (female)"]
  J3 = female pin header, 6 pins [form="♀ (female)"]
  J4 = female pin header, 6 pins [form="♀ (female)"]  # not connected
  Redbear_DUO = IC, DIP package, 24 pins [chip_label="Redbear DUO"]
  J5 = female pin header, 4 pins [form="♀ (female)"]  # not connected
  BLE_Nano = IC, DIP package, 12 pins [chip_label="BLE Nano"]
  J6 = female pin header, 12 pins [form="♀ (female)"]  # not connected
  J7 = female pin header, 12 pins [form="♀ (female)"]  # not connected
  J8 = female pin header, 6 pins [form="♀ (female)"]
  J9 = female pin header, 6 pins [form="♀ (female)"]
  J10 = female pin header, 4 pins [form="♀ (female)"]
  BLE_Nano1 = IC, DIP package, 12 pins [chip_label="BLE Nano"]  # not connected
  Redbear_DUO1 = IC, DIP package, 24 pins [chip_label="Redbear DUO"]

nets:
  N1: J1.pin7, BLE_Nano.pin2
  N2: J2.pin2, J3.pin2
  N3: J2.pin4, BLE_Nano.pin3
  N4: Redbear_DUO.pin5, BLE_Nano.pin5
  N5: Redbear_DUO.pin10, BLE_Nano.pin4
  N6: Redbear_DUO.pin11, BLE_Nano.pin6
  N7: Redbear_DUO.pin15, BLE_Nano.pin9
  N8: Redbear_DUO.pin20, BLE_Nano.pin8
  N9: J8.pin5, J10.pin3
  N10: J8.pin6, J10.pin4
  N11: J9.pin1, Redbear_DUO1.pin7
  N12: J9.pin2, Redbear_DUO1.pin5
  N13: J9.pin3, Redbear_DUO1.pin3
  N14: J9.pin4, Redbear_DUO1.pin1

notes:
  5V, GND, RX, TX
  TX, RX, GND, 5V
  Antennas (DUO and Nano) point to the bottom
  Antennas (DUO and Nano) point to the left
